// Logisim project Computer.circ as structural Verilog
module GeneralPurposeRegister (
  input  [7:0] MB,
  input  [3:0] RCB,
  input  [3:0] SYS,
  output [7:0] TXLB,
  output [7:0] TXHB
);

  wire and_1_out, and_2_out, not_1_out, not_2_out, not_3_out, or_1_out;
  wire [7:0] controlled_buffer_1_out, controlled_buffer_4_out, controlled_buffer_5_out, register_1_q;

  Pull_Resistor pull_resistor_1 (.node(SYS[2]));
  not not_1 (not_1_out, RCB[1]);
  and and_1 (and_1_out, RCB[2], not_1_out);
  or or_1 (or_1_out, RCB[1], RCB[0]);
  and and_2 (and_2_out, not_1_out, RCB[3]);
  assign controlled_buffer_1_out = RCB[2] ? TXLB : 8'bz;  // Controlled_Buffer controlled_buffer_1
  assign controlled_buffer_1_out = RCB[3] ? TXHB : 8'bz;  // Controlled_Buffer controlled_buffer_2
  assign controlled_buffer_1_out = RCB[0] ? MB : 8'bz;  // Controlled_Buffer controlled_buffer_3
  assign controlled_buffer_4_out = or_1_out ? controlled_buffer_1_out : 8'bz;  // Controlled_Buffer controlled_buffer_4
  not not_2 (not_2_out, SYS[1]);
  Register register_1 (.D(controlled_buffer_4_out), .en(or_1_out), .clk(not_2_out), .Q(register_1_q));  // open: clr
  assign controlled_buffer_5_out = not_3_out ? MB : 8'bz;  // Controlled_Buffer controlled_buffer_5
  not not_3 (not_3_out, RCB[0]);
  assign controlled_buffer_5_out = not_3_out ? register_1_q : 8'bz;  // Controlled_Buffer controlled_buffer_6
  assign TXHB = and_2_out ? controlled_buffer_5_out : 8'bz;  // Controlled_Buffer controlled_buffer_7
  assign TXLB = and_1_out ? controlled_buffer_5_out : 8'bz;  // Controlled_Buffer controlled_buffer_8
  // also tied to GND on the sheet: SYS[3]
  // also tied to VCC on the sheet: SYS[0]

  // Notes on the sheet:
  //   TXLB: pull=down
  //   TXHB: pull=down
  //   Transfer Bus (Lower)
  //   Transfer Bus (Higher)
  //   Main Bus
  //   Register Control Bus
  //   System Bus
endmodule
